# Fritzing sketch Makerfest 2019 (saved by Fritzing 0.9.3b)
breadboards: 2

parts:
  Part4 = Thumb Joystick  # not connected
  Part3 = Arduino Micro (Rev3)
  R1 = Resistor [tolerance=±5% resistance=220 package=THT]
  R2 = Resistor [tolerance=±5% resistance=220 package=THT]
  S1 = Round Pushbutton
  S2 = Round Pushbutton

nets:
  N1: Part3.D2/SDA, R1.Pin_0, S1.leg1
  N2: Part3.D3/SCL, R2.Pin_0, S2.leg0
  N3: R1.Pin_1, R2.Pin_1
  N4: S1.leg0, S2.leg1
